# Fritzing sketch GarageDoorMonitor (saved by Fritzing 0.9.10b)
breadboards: 1

parts:
  Part1 = Arduino Pro Mini (5V)
  HC-SR04_Sensor_1 = HC-SR04 Ultrasonic Distance Sensor
  Part2 = FTDI Basic Programmer
  J2 = Power Jack [package=power_jack_combo]
  R1_Pull_up = Resistor [tolerance=±5% power=0.25 resistance=10k package=THT]
  P1 = Multimeter straight black probe
  Ground_for_Debug = Multimeter straight red probe
  Relay_Normally_Open = KY-019 5V Relay Module [package="Breakout board"]
  Wire_to_Garage_Switch_in_parallel = Screw terminal - 2 pins [package=THT]

nets:
  N1: Part1.DTR, Part2.DTR
  N2: Part1.TXO, Part2.RXI
  N3: Part1.RXI, Part2.TXO
  5V: Part1.VCC, Part2.POWER, R1_Pull_up.Pin_0, Relay_Normally_Open.+
  GND: Part1.GND, HC-SR04_Sensor_1.GND, Part2.CTS, Part2.GND, J2.GND, J2.GNDBREAK, P1.Probe_meter_end, P1.Probe_tip_2, Relay_Normally_Open.-
  N4: Part1.RAW, J2.PWR
  N5: Part1.D5, R1_Pull_up.Pin_1, Ground_for_Debug.Probe_tip, Ground_for_Debug.Probe_meter_end
  N6: Part1.D4, Relay_Normally_Open.S
  N7: Part1.D3, HC-SR04_Sensor_1.ECHO
  N8: Part1.D2, HC-SR04_Sensor_1.TRIG
  N9: Relay_Normally_Open.Common, Wire_to_Garage_Switch_in_parallel.pin1
  N10: Relay_Normally_Open.NO, Wire_to_Garage_Switch_in_parallel.pin2

notes:
  Garage Door Monitor
  Using the HC-SR04 as a sensor.
  Released into the public domain in the hopes it will be useful.
  But use at your own risk.
  Mark L. Martin
  1/1/2023
  Happy new year

custom parts:
  KY-019 5V Relay Module: KY-019 5V Relay module, used to control AC circuits.
